// Digital circuit pcv1.dig as structural Verilog
module pcv1 (
  input  in_1,
  input  in_2,
  input  in_3,
  input  in_4,
  input  in_5,
  input  in_6,
  input  in_7,
  input  in_8,
  input  in_9,
  input  in_10,
  input  in_11,
  input  in_12,
  input  in_13,
  input  in_14,
  input  in_15,
  input  in_16,
  input  in_17,
  input  in_18,
  input  in_19,
  input  in_20,
  input  in_21,
  input  in_22,
  input  in_23,
  input  in_24,
  input  in_25,
  input  in_26,
  input  in_27,
  input  in_28,
  input  in_29,
  input  in_30,
  input  in_31,
  input  in_32,
  input  in_33,
  input  in_34,
  input  in_35
);

  wire and_1_out, and_2_out, and_3_out, and_4_out, and_5_out, and_6_out, and_7_out, and_8_out, and_9_out,
       and_10_out, and_11_out, and_12_out, and_13_out, and_14_out, and_15_out, and_16_out, and_17_out,
       and_18_out, and_19_out, and_20_out, and_21_out, and_22_out, and_23_out, and_24_out, and_25_out,
       and_26_out, and_27_out, and_28_out, and_29_out, and_30_out, and_31_out, and_32_out, and_33_out,
       and_34_out, and_35_out, and_36_out, and_37_out, and_38_out, and_39_out, and_40_out, and_41_out,
       and_42_out, and_43_out, and_44_out, and_45_out, and_46_out, and_47_out, and_48_out, or_1_out,
       or_2_out, or_3_out, or_4_out, or_5_out, or_6_out, or_7_out, or_8_out, or_9_out, or_10_out, or_11_out,
       or_12_out, or_13_out, or_14_out, or_15_out, or_16_out, xor_1_out, xor_2_out, xor_3_out, xor_4_out,
       xor_5_out, xor_6_out, xor_7_out, xor_8_out, xor_9_out, xor_10_out, xor_11_out, xor_12_out, xor_13_out,
       xor_14_out, xor_15_out, xor_16_out, xor_17_out, xor_18_out, xor_19_out, xor_20_out, xor_21_out,
       xor_22_out, xor_23_out, xor_24_out, xor_25_out, xor_26_out, xor_27_out, xor_28_out, xor_29_out,
       xor_30_out, xor_31_out, xor_32_out;

  and and_1 (and_1_out, in_1, in_2);
  and and_2 (and_2_out, in_1, in_17);
  and and_3 (and_3_out, in_2, in_17);
  and and_4 (and_4_out, or_1_out, in_3);
  and and_5 (and_5_out, or_1_out, in_18);
  and and_6 (and_6_out, in_3, in_18);
  and and_7 (and_7_out, or_2_out, in_4);
  and and_8 (and_8_out, or_2_out, in_19);
  and and_9 (and_9_out, in_4, in_19);
  and and_10 (and_10_out, or_3_out, in_5);
  and and_11 (and_11_out, or_3_out, in_20);
  and and_12 (and_12_out, in_5, in_20);
  and and_13 (and_13_out, or_4_out, in_6);
  and and_14 (and_14_out, or_4_out, in_21);
  and and_15 (and_15_out, in_6, in_21);
  and and_16 (and_16_out, or_5_out, in_7);
  and and_17 (and_17_out, or_5_out, in_22);
  and and_18 (and_18_out, in_7, in_22);
  and and_19 (and_19_out, or_6_out, in_8);
  and and_20 (and_20_out, or_6_out, in_25);
  and and_21 (and_21_out, in_8, in_25);
  and and_22 (and_22_out, or_7_out, in_9);
  and and_23 (and_23_out, or_7_out, in_23);
  and and_24 (and_24_out, in_9, in_23);
  and and_25 (and_25_out, or_8_out, in_10);
  and and_26 (and_26_out, or_8_out, in_26);
  and and_27 (and_27_out, in_10, in_26);
  and and_28 (and_28_out, or_9_out, in_11);
  and and_29 (and_29_out, or_9_out, in_27);
  and and_30 (and_30_out, in_11, in_27);
  and and_31 (and_31_out, or_10_out, in_12);
  and and_32 (and_32_out, or_10_out, in_29);
  and and_33 (and_33_out, in_12, in_29);
  and and_34 (and_34_out, or_11_out, in_13);
  and and_35 (and_35_out, or_11_out, in_28);
  and and_36 (and_36_out, in_13, in_28);
  and and_37 (and_37_out, or_12_out, in_14);
  and and_38 (and_38_out, or_12_out, in_30);
  and and_39 (and_39_out, in_14, in_30);
  and and_40 (and_40_out, or_13_out, in_15);
  and and_41 (and_41_out, or_13_out, in_31);
  and and_42 (and_42_out, in_15, in_31);
  and and_43 (and_43_out, or_14_out, in_16);
  and and_44 (and_44_out, or_14_out, in_32);
  and and_45 (and_45_out, in_16, in_32);
  and and_46 (and_46_out, or_15_out, in_35);
  and and_47 (and_47_out, or_15_out, in_34);
  and and_48 (and_48_out, in_35, in_34);
  or or_1 (or_1_out, and_1_out, and_2_out, and_3_out);
  or or_2 (or_2_out, and_4_out, and_5_out, and_6_out);
  or or_3 (or_3_out, and_7_out, and_8_out, and_9_out);
  or or_4 (or_4_out, and_10_out, and_11_out, and_12_out);
  or or_5 (or_5_out, and_13_out, and_14_out, and_15_out);
  or or_6 (or_6_out, and_16_out, and_17_out, and_18_out);
  or or_7 (or_7_out, and_19_out, and_20_out, and_21_out);
  or or_8 (or_8_out, and_22_out, and_23_out, and_24_out);
  or or_9 (or_9_out, and_25_out, and_26_out, and_27_out);
  or or_10 (or_10_out, and_28_out, and_29_out, and_30_out);
  or or_11 (or_11_out, and_31_out, and_32_out, and_33_out);
  or or_12 (or_12_out, and_34_out, and_35_out, and_36_out);
  or or_13 (or_13_out, and_37_out, and_38_out, and_39_out);
  or or_14 (or_14_out, and_40_out, and_41_out, and_42_out);
  or or_15 (or_15_out, and_43_out, and_44_out, and_45_out);
  or or_16 (or_16_out, and_46_out, and_47_out, and_48_out);
  xor xor_1 (xor_1_out, in_2, in_17);
  xor xor_2 (xor_2_out, in_3, in_18);
  xor xor_3 (xor_3_out, in_4, in_19);
  xor xor_4 (xor_4_out, in_5, in_20);
  xor xor_5 (xor_5_out, in_6, in_21);
  xor xor_6 (xor_6_out, in_7, in_22);
  xor xor_7 (xor_7_out, in_8, in_25);
  xor xor_8 (xor_8_out, in_9, in_23);
  xor xor_9 (xor_9_out, in_10, in_26);
  xor xor_10 (xor_10_out, in_11, in_27);
  xor xor_11 (xor_11_out, in_12, in_29);
  xor xor_12 (xor_12_out, in_13, in_28);
  xor xor_13 (xor_13_out, in_14, in_30);
  xor xor_14 (xor_14_out, in_15, in_31);
  xor xor_15 (xor_15_out, in_16, in_32);
  xor xor_16 (xor_16_out, in_35, in_34);
  xor xor_17 (xor_17_out, xor_1_out, in_1);
  xor xor_18 (xor_18_out, xor_2_out, or_1_out);
  xor xor_19 (xor_19_out, xor_3_out, or_2_out);
  xor xor_20 (xor_20_out, xor_4_out, or_3_out);
  xor xor_21 (xor_21_out, xor_5_out, or_4_out);
  xor xor_22 (xor_22_out, xor_6_out, or_5_out);
  xor xor_23 (xor_23_out, xor_7_out, or_6_out);
  xor xor_24 (xor_24_out, xor_8_out, or_7_out);
  xor xor_25 (xor_25_out, xor_9_out, or_8_out);
  xor xor_26 (xor_26_out, xor_10_out, or_9_out);
  xor xor_27 (xor_27_out, xor_11_out, or_10_out);
  xor xor_28 (xor_28_out, xor_12_out, or_11_out);
  xor xor_29 (xor_29_out, xor_13_out, or_12_out);
  xor xor_30 (xor_30_out, xor_14_out, or_13_out);
  xor xor_31 (xor_31_out, xor_15_out, or_14_out);
  xor xor_32 (xor_32_out, xor_16_out, or_15_out);

  assign in_24 = in_22;
  assign in_33 = in_32;
endmodule
